// Logisim project CPULib.circ as structural Verilog: 5 circuits, main circuit CPU
module CPU (
  input  [15:0] ins,
  input  [15:0] inM,
  input  clk,
  input  reset,
  output [15:0] outM,
  output writeM,
  output [15:0] addressM,
  output [15:0] counter
);

  wire aluammuxctl_1_o, aregloadctl_1_o, aregmuxctl_1_out_2;
  wire [15:0] A_q, D_q, multiplexer_1_out, multiplexer_2_out;

  ARegMuxCtl aregmuxctl_1 (.in_1(ins), .out_2(aregmuxctl_1_out_2));
  Multiplexer #(.width(16)) multiplexer_1 (.in0(ins), .in1(outM), .out(multiplexer_1_out), .sel(aregmuxctl_1_out_2));
  ARegLoadCtl aregloadctl_1 (.instln(ins), .o(aregloadctl_1_o));
  Reg16 A (.load(aregloadctl_1_o), .D(multiplexer_1_out), .Q(A_q));  // open: clk
  Multiplexer #(.width(16)) multiplexer_2 (.in0(A_q), .in1(inM), .out(multiplexer_2_out), .sel(aluammuxctl_1_o));
  ALUAMMuxCtl aluammuxctl_1 (.instln(ins), .o(aluammuxctl_1_o));
  Reg16 D (.D(outM), .Q(D_q));  // open: load, clk
  ALU alu_1 (.x(multiplexer_2_out), .y(D_q));  // open: zx, nx, f, zy, ny, no, o, zr, ng
  // PC pc_1: pin names not known

  // Other names for the same wires on the sheet: clock = clk
endmodule

module ARegMuxCtl (
  input  [15:0] in_1,
  output out_2
);


  assign out_2 = in_1[15];
endmodule

module ARegLoadCtl (
  input  [15:0] instln,
  output o
);

  wire and_1_out, not_1_out;

  and and_1 (and_1_out, instln[5], instln[15]);
  not not_1 (not_1_out, instln[15]);
  or or_1 (o, and_1_out, not_1_out);
endmodule

module ALUAMMuxCtl (
  input  [15:0] instln,
  output o
);

  wire not_1_out;

  not not_1 (not_1_out, instln[12]);
  and and_1 (o, not_1_out, instln[15]);
endmodule

module DRegLoadCtl (
  input  [15:0] instln,
  output [15:0] o
);
endmodule
